// Digital circuit 2c.dig as structural Verilog
module _2c (
  input  [7:0] A,
  output [7:0] X,
  output Cout
);

  wire add8b_1_cout;
  wire [7:0] not_1_out;

  assign not_1_out = ~A;  // Not not_1, 8 bits wide
  add8b add8b_1 (.A(not_1_out), .B(8'h1), .Cin(1'b0), .X(X), .Cout(add8b_1_cout));
  nor nor_1 (Cout, add8b_1_cout, A[7]);
endmodule
