// Digital circuit min8b.dig as structural Verilog
module min8b (
  input  [7:0] A,
  input  [7:0] B,
  input  Cin,
  output [7:0] X,
  output Cout
);

  wire [7:0] _2c_1_x;

  _2c _2c_1 (.A(B), .Cin(Cin), .X(_2c_1_x));  // open: Cout
  add8b add8b_1 (.A(A), .B(_2c_1_x), .Cin(Cin), .X(X), .Cout(Cout));
endmodule
